# Fritzing sketch Esquemas de conexiones (saved by Fritzing 0.8.7b)
breadboards: 2

parts:
  BREAKOUT1 = ULN2003A breakout board
  BREAKOUT2 = ULN2003A breakout board
  MOTOR2 = 28BYJ-48 Stepper Motor
  MOTOR3 = 28BYJ-48 Stepper Motor
  Componente1 = Arduino Mega 2560 (Rev3)
  R1 = Rotary Potentiometer (Small) [maximum_resistance=10kΩ package=THT]
  R3 = Rotary Potentiometer (Small) [maximum_resistance=10kΩ package=THT]
  R4 = Rotary Potentiometer (Small) [maximum_resistance=10kΩ package=THT]
  R5 = Rotary Potentiometer (Small) [maximum_resistance=10kΩ package=THT]
  BREAKOUT3 = ULN2003A breakout board
  MOTOR4 = 28BYJ-48 Stepper Motor
  J1 = Basic Servo
  Power_plug1 = Power plug
  D2F1 = D2F-FL Omron Snap Action Limit Switch with Level
  D2F2 = D2F-FL Omron Snap Action Limit Switch with Level
  S1 = Pushbutton [package="[THT]"]
  R6 = Resistor [tolerance=±5% resistance=10k package=THT]
  Parte2 = Bluetooth HC-05 Macho

nets:
  N1: BREAKOUT1.In_1, Componente1.D30
  N2: BREAKOUT1.In_2, Componente1.D32
  N3: BREAKOUT1.In_3, Componente1.D34
  N4: BREAKOUT1.In_4, Componente1.D36
  N5: BREAKOUT1.0V, BREAKOUT2.0V, BREAKOUT3.0V, Power_plug1.GND
  +5V: BREAKOUT1.+5V, BREAKOUT2.+5V, BREAKOUT3.+5V, BREAKOUT3.ON/OFF_jumper_switch, Power_plug1.VCC
  N6: BREAKOUT1.RED_wire, MOTOR4.RED
  N7: BREAKOUT1.ORANGE_wire, MOTOR4.ORANGE
  N8: BREAKOUT1.YELLOW_wire, MOTOR4.YELLOW
  N9: BREAKOUT1.PINK_wire, MOTOR4.PINK
  N10: BREAKOUT1.BLUE_wire, MOTOR4.BLUE
  N11: BREAKOUT2.In_1, Componente1.D42
  N12: BREAKOUT2.In_2, Componente1.D44
  N13: BREAKOUT2.In_3, Componente1.D46
  N14: BREAKOUT2.In_4, Componente1.D48
  N15: BREAKOUT2.RED_wire, MOTOR2.RED
  N16: BREAKOUT2.ORANGE_wire, MOTOR2.ORANGE
  N17: BREAKOUT2.YELLOW_wire, MOTOR2.YELLOW
  N18: BREAKOUT2.PINK_wire, MOTOR2.PINK
  N19: BREAKOUT2.BLUE_wire, MOTOR2.BLUE
  N20: MOTOR3.RED, BREAKOUT3.RED_wire
  N21: MOTOR3.ORANGE, BREAKOUT3.ORANGE_wire
  N22: MOTOR3.YELLOW, BREAKOUT3.YELLOW_wire
  N23: MOTOR3.PINK, BREAKOUT3.PINK_wire
  N24: MOTOR3.BLUE, BREAKOUT3.BLUE_wire
  N25: Componente1.A0, R3.wiper
  N26: Componente1.A1, R5.wiper
  N27: Componente1.A2, R4.wiper
  N28: Componente1.A3, R1.wiper
  GND: Componente1.GND, R1.leg1, R3.leg1, R4.leg1, R5.leg1, J1.gnd, D2F1.COM, D2F2.COM, R6.Pin_1, Parte2.GND
  VCC: Componente1.5V, R1.leg2, R3.leg2, R4.leg2, R5.leg2, J1.vcc, S1.Pin_3, S1.Pin_4, Parte2.VCC
  N29: Componente1.D0_RX0, Parte2.TXD
  N30: Componente1.D1_TX0, Parte2.RXD
  N31: Componente1.D2_PWM, J1.pulse
  N32: Componente1.D3_PWM, D2F1.NC
  N33: Componente1.D4_PWM, D2F2.NC
  N34: Componente1.D5_PWM, S1.Pin_1, S1.Pin_2, R6.Pin_0
  N35: Componente1.D22, BREAKOUT3.In_1
  N36: Componente1.D24, BREAKOUT3.In_2
  N37: Componente1.D26, BREAKOUT3.In_3
  N38: Componente1.D28, BREAKOUT3.In_4

custom parts:
  ULN2003A breakout board: ULN2003A 7-way Darlington Transistor Driver on breakoutboard
  D2F-FL Omron Snap Action Limit Switch with Level: Snap action switch with stainless steel lever.

// code stored in the sketch: Untitled2.ino

